# Fritzing sketch PCB_compactadora_bak (saved by Fritzing 0.9.3b)
breadboards: 1

parts:
  Componente1 = Arduino Mega 2560 (Rev3)  # not connected
  Load_Cell = IC, SIP package, 4 pins [chip_label=LC]  # not connected
  Door_sensor = Resistor [tolerance=±5% resistance=1 package="0805 [SMD]"]  # not connected
  S1 = Round Pushbutton  # not connected
  S2 = Round Pushbutton  # not connected
  J1 = Piezo Speaker  # not connected
  S3 = Toggle Switch [package=THT]  # not connected
  LED2 = LED - 3mm [color="Red (633nm)" package="3 mm [THT]"]
  R1 = Resistor [tolerance=±5% resistance=1k package="2512 [SMD]"]
  LED1 = LED - 3mm [color="Red (633nm)" package="3 mm [THT]"]
  R2 = Resistor [tolerance=±5% resistance=1k package="2512 [SMD]"]
  NX8048K070 = IC, SIP package, 4 pins [chip_label=NXT]  # not connected
  Load_Cell3 = Load Cell - Red/white/black/green
  Part5 = HX711 Weighing Sensor Module

nets:
  N1: LED2.anode, R2.Pin_0
  N2: R1.Pin_0, LED1.anode
  N3: Load_Cell3.wire1, Part5.E+
  N4: Load_Cell3.wire2, Part5.A+
  N5: Load_Cell3.wire3, Part5.E-
  N6: Load_Cell3.wire4, Part5.A-

custom parts:
  Load Cell - Red/white/black/green: A rectangle load cell/weighting pressure Sensor with four wires - Red, white, black, green. Normally corresponding with E+, E-, A+, A- respectively.
  HX711 Weighing Sensor Module: HX711 is a precision 24-bit analog-to-digital converter (ADC) designed for weigh scales and industrial control applications to interface directly with a bridge sensor.
