# Fritzing sketch arduino-hx711-load-cell (saved by Fritzing 0.9.3b)

parts:
  Load_Cell2 = Load Cell - Red/white/black/green
  Part4 = HX711 Weighing Sensor Module

nets:
  N1: Load_Cell2.wire1, Part4.E+
  N2: Load_Cell2.wire2, Part4.A+
  N3: Load_Cell2.wire3, Part4.E-
  N4: Load_Cell2.wire4, Part4.A-

custom parts:
  Load Cell - Red/white/black/green: A rectangle load cell/weighting pressure Sensor with four wires - Red, white, black, green. Normally corresponding with E+, E-, A+, A- respectively.
  HX711 Weighing Sensor Module: HX711 is a precision 24-bit analog-to-digital converter (ADC) designed for weigh scales and industrial control applications to interface directly with a bridge sensor.
